// Logisim project Project1_oefening5.circ as structural Verilog: 2 circuits, main circuit main
module main (
  input  [2:0] X
);

  wire A_out, and_1_out, and_2_out, and_3_out, and_4_out, and_5_out, and_6_out, and_7_out, and_8_out,
       and_9_out, and_10_out, and_11_out, and_12_out, and_13_out, and_14_out, and_15_out, and_16_out,
       and_17_out, and_18_out, and_19_out, and_20_out, and_21_out, and_22_out, and_23_out, and_24_out,
       and_25_out, and_26_out, and_27_out, and_28_out, and_29_out, and_30_out, and_31_out, and_32_out,
       and_33_out, and_34_out, and_35_out, and_36_out, B_out, C_out, D_out, E_out, F_out, G_out, not_1_out,
       not_2_out, not_3_out;

  _7_Segment_Display u_7_segment_display_1 (
    .g(G_out), .f(F_out), .a(A_out), .b(B_out), .e(E_out), .d(D_out), .c(C_out));  // open: dp
  not not_1 (not_1_out, X[2]);
  not not_2 (not_2_out, X[1]);
  not not_3 (not_3_out, X[0]);
  and and_1 (and_1_out, not_1_out, not_2_out, not_3_out);
  and and_2 (and_2_out, not_1_out, X[1], not_3_out);
  and and_3 (and_3_out, not_1_out, X[1], X[0]);
  or A (A_out, and_1_out, and_2_out, and_3_out, and_4_out, and_5_out, and_6_out);
  and and_4 (and_4_out, X[2], not_2_out, X[0]);
  and and_5 (and_5_out, X[2], X[1], not_3_out);
  and and_6 (and_6_out, X[2], X[1], X[0]);
  and and_7 (and_7_out, not_1_out, not_2_out, not_3_out);
  and and_8 (and_8_out, not_1_out, not_2_out, X[0]);
  and and_9 (and_9_out, not_1_out, X[1], not_3_out);
  or B (B_out, and_7_out, and_8_out, and_9_out, and_10_out, and_11_out, and_12_out);
  and and_10 (and_10_out, not_1_out, X[1], X[0]);
  and and_11 (and_11_out, X[2], not_2_out, not_3_out);
  and and_12 (and_12_out, X[2], X[1], X[0]);
  and and_13 (and_13_out, not_1_out, not_2_out, not_3_out);
  and and_14 (and_14_out, not_1_out, not_2_out, X[0]);
  and and_15 (and_15_out, not_1_out, X[1], X[0]);
  and and_16 (and_16_out, X[2], not_2_out, not_3_out);
  or C (C_out, and_13_out, and_14_out, and_15_out, and_16_out, and_17_out, and_18_out, and_19_out);
  and and_17 (and_17_out, X[2], not_2_out, X[0]);
  and and_18 (and_18_out, X[2], X[1], not_3_out);
  and and_19 (and_19_out, X[2], X[1], X[0]);
  and and_20 (and_20_out, not_1_out, not_2_out, not_3_out);
  and and_21 (and_21_out, not_1_out, X[1], not_3_out);
  and and_22 (and_22_out, not_1_out, X[1], X[0]);
  or D (D_out, and_20_out, and_21_out, and_22_out, and_23_out, and_24_out);
  and and_23 (and_23_out, X[2], not_2_out, X[0]);
  and and_24 (and_24_out, X[2], X[1], not_3_out);
  and and_25 (and_25_out, not_1_out, X[1], not_3_out);
  and and_26 (and_26_out, not_1_out, not_2_out, not_3_out);
  and and_27 (and_27_out, X[2], X[1], not_3_out);
  or E (E_out, and_26_out, and_25_out, and_27_out);
  and and_28 (and_28_out, not_1_out, not_2_out, not_3_out);
  and and_29 (and_29_out, X[2], not_2_out, not_3_out);
  or F (F_out, and_28_out, and_29_out, and_30_out, and_31_out);
  and and_30 (and_30_out, X[2], not_2_out, X[0]);
  and and_31 (and_31_out, X[2], X[1], not_3_out);
  and and_32 (and_32_out, not_1_out, X[1], not_3_out);
  and and_33 (and_33_out, not_1_out, X[1], X[0]);
  and and_34 (and_34_out, X[2], not_2_out, not_3_out);
  and and_35 (and_35_out, X[2], not_2_out, X[0]);
  or G (G_out, and_32_out, and_33_out, and_34_out, and_35_out, and_36_out);
  and and_36 (and_36_out, X[2], X[1], not_3_out);

  // Notes on the sheet:
  //   X: pull=down
  //   X
  //   Y
  //   Z
endmodule

module kleiner (
  input  [2:0] X,
  output A,
  output B,
  output C,
  output D,
  output E,
  output F,
  output G
);

  wire _0_out, _1_out, _2_out, _4_out, _5_out, _6_out, _7_out, not_1_out, not_2_out, not_3_out;

  not not_1 (not_1_out, X[2]);
  not not_2 (not_2_out, X[1]);
  not not_3 (not_3_out, X[0]);
  and _0 (_0_out, not_3_out, not_2_out, not_1_out);
  and _1 (_1_out, X[0], not_2_out, not_1_out);
  nor nor_1 (A, _1_out, _4_out);
  nor nor_2 (B, _5_out, _6_out);
  _7_Segment_Display u_7_segment_display_1 (.g(G), .f(F), .a(A), .b(B), .e(E), .d(D), .c(C));  // open: dp
  // AND_Gate _3 has open pins: in0=X[0], in1=X[1], in2=not_1_out, out=open
  and _2 (_2_out, not_3_out, X[1], not_1_out);
  not not_4 (C, _2_out);
  nor nor_3 (D, _1_out, _4_out, _7_out);
  and _5 (_5_out, X[2], not_2_out, X[0]);
  and _4 (_4_out, X[2], not_2_out, not_3_out);
  or or_1 (F, _0_out, _4_out, _5_out, _6_out);
  or or_2 (E, _0_out, _2_out, _6_out);
  and _7 (_7_out, X[2], X[1], X[0]);
  and _6 (_6_out, not_3_out, X[2], X[1]);
  nor nor_4 (G, _0_out, _1_out, _7_out);

  // Notes on the sheet:
  //   X: pull=down
  //   X
  //   Y
  //   Z
endmodule
