// Logisim project project 1_oefening3 .circ as structural Verilog: 1 circuit, main circuit main
module main (
  input  in_1,
  input  in_2,
  input  in_3,
  input  in_4,
  input  in_5,
  input  in_6,
  input  in_7,
  input  in_8,
  input  in_9,
  output out_10,
  output out_11,
  output out_12,
  output out_13,
  output out_14
);

  wire and_1_out, nand_1_out, nand_3_out, nand_4_out, not_1_out, not_2_out;

  and and_1 (and_1_out, in_1, in_3);
  not not_1 (not_1_out, in_5);
  not not_2 (not_2_out, in_6);
  not not_3 (out_10, and_1_out);
  or or_1 (out_12, not_1_out, not_2_out);
  nand nand_1 (nand_1_out, in_2, in_4);
  nand nand_2 (out_13, in_7, in_7);
  nand nand_3 (nand_3_out, in_8, in_8);
  nand nand_4 (nand_4_out, in_9, in_9);
  nand nand_5 (out_11, nand_1_out, nand_1_out);
  nand nand_6 (out_14, nand_3_out, nand_4_out);

  // Notes on the sheet:
  //   NAND poort Manier 1 
  //   NAND poort Manier 2
  //   AND GATE
  //   OR GATE
  //   NOT GATE
endmodule
