// Logisim project ALU_Group33.circ as structural Verilog: 19 circuits, main circuit main
module main (
  output halt,
  output [12:0] counter,
  output [3:0] op,
  output [11:0] a,
  output [11:0] b,
  output [11:0] oracle,
  output [11:0] result,
  output err_oracle,
  output error,
  output ok,
  output start_delimiter
);

  wire and_1_out, and_2_out, clock_1_out, comparator_1_eq, comparator_2_eq;

  Clock clock_1 (.out(clock_1_out));
  Counter #(.width(13), .max('h1fff), .trigger("falling")) counter_1 (
    .Q(counter), .carry(halt), .clk(clock_1_out));  // open: load, D, count, clr
  RAM #(.addrWidth(16), .dataWidth(4), .bus("separate")) ram_1 (
    .addr({counter, 3'b000}), .data(op), .ld(1'b1));  // open: din, str, sel, clk, clr
  RAM #(.addrWidth(16), .dataWidth(12), .bus("separate")) ram_2 (
    .addr({counter, 3'b001}), .data(a), .ld(1'b1));  // open: din, str, sel, clk, clr
  RAM #(.addrWidth(16), .dataWidth(12), .bus("separate")) ram_3 (
    .addr({counter, 3'b010}), .data(b), .ld(1'b1));  // open: din, str, sel, clk, clr
  RAM #(.addrWidth(16), .dataWidth(12), .bus("separate")) ram_4 (
    .addr({counter, 3'b011}), .data(oracle), .ld(1'b1));  // open: din, str, sel, clk, clr
  RAM #(.addrWidth(16), .dataWidth(1), .bus("separate")) ram_5 (
    .addr({counter, 3'b100}), .data(err_oracle), .ld(1'b1));  // open: din, str, sel, clk, clr
  RAM #(.addrWidth(16), .dataWidth(1), .bus("separate")) ram_6 (
    .addr({counter, 3'b101}), .data(start_delimiter), .ld(1'b1));  // open: din, str, sel, clk, clr
  _12_bit_ALU u_12_bit_alu_1 (.ALU_code(op), .a(a), .b(b), .overflow(error), .result(result));
  Comparator #(.width(1), .mode("unsigned")) comparator_1 (
    .a(error), .b(err_oracle), .eq(comparator_1_eq));  // open: gt, lt
  Comparator #(.width(12)) comparator_2 (.a(result), .b(oracle), .eq(comparator_2_eq));  // open: gt, lt
  and and_1 (and_1_out, comparator_1_eq, error);
  and and_2 (and_2_out, comparator_2_eq, comparator_1_eq, ~error);  // AND_Gate
  or or_1 (ok, and_1_out, and_2_out);

  // Notes on the sheet:
  //   You must complete the circuit '12-bit ALU' instead.
  //   DO NOT EDIT THIS CIRCUIT!
endmodule

module _12_bit_ALU (
  input  [3:0] ALU_code,
  input  [11:0] a,
  input  [11:0] b,
  output [11:0] result,
  output overflow
);

  wire ADD_overflow, invert_overflow, SLA_overflow, SUB_overflow;
  wire [11:0] _0_out_1, ADD_out_3, AND_out_3, EQ_out_3, GT_out_3, invert_out_2, LT_out_3, NEQ_out_3,
       NO_OP_out_2, NOT_out_2, OR_out_3, SLA_out_3, SLL_out_2, SRA_out_2, SRL_out_2, SUB_out_3;

  // Probe on a
  // Probe on b
  GEN_0 _0 (.out_1(_0_out_1));
  NOT NOT (.in_1(a), .out_2(NOT_out_2));
  AND AND (.in_1(a), .in_2(b), .out_3(AND_out_3));
  OR OR (.in_1(a), .in_2(b), .out_3(OR_out_3));
  ADD ADD (.in_1(a), .in_2(b), .out_3(ADD_out_3), .OVERFLOW(ADD_overflow));
  SUB SUB (.in_1(a), .in_2(b), .out_3(SUB_out_3), .overflow(SUB_overflow));
  LT LT (.in_1(a), .in_2(b), .out_3(LT_out_3));
  GT GT (.in_1(a), .in_2(b), .out_3(GT_out_3));
  eq EQ (.in_1(a), .in_2(b), .out_3(EQ_out_3));
  neq NEQ (.in_1(a), .in_2(b), .out_3(NEQ_out_3));
  INVERT invert (.in_1(a), .overflow(invert_overflow), .out_2(invert_out_2));
  SLL SLL (.in_1(a), .out_2(SLL_out_2));
  SRL SRL (.in_1(a), .out_2(SRL_out_2));
  SLA SLA (.in_1(a), .overflow(SLA_overflow), .out_3(SLA_out_3));
  SRA SRA (.in_1(a), .out_2(SRA_out_2));
  NO_OP NO_OP (.in_1(a), .out_2(NO_OP_out_2));
  Multiplexer #(.select(4)) multiplexer_1 (
    .in0(1'b0), .in1(1'b0), .in2(1'b0), .in3(1'b0), .in4(ADD_overflow), .in5(SUB_overflow), .in6(1'b0),
    .in7(1'b0), .in8(1'b0), .in9(1'b0), .in10(invert_overflow), .in11(1'b0), .in12(1'b0),
    .in13(SLA_overflow), .in14(1'b0), .in15(1'b0), .out(overflow), .sel(ALU_code));  // open: en
  Multiplexer #(.select(4), .width(12)) multiplexer_2 (
    .in0(_0_out_1), .in1(NOT_out_2), .in2(AND_out_3), .in3(OR_out_3), .in4(ADD_out_3), .in5(SUB_out_3),
    .in6(LT_out_3), .in7(GT_out_3), .in8(EQ_out_3), .in9(NEQ_out_3), .in10(invert_out_2), .in11(SLL_out_2),
    .in12(SRL_out_2), .in13(SLA_out_3), .in14(SRA_out_2), .in15(NO_OP_out_2), .out(result), .sel(ALU_code));  // open: en

  // Other names for the same wires on the sheet: ALU[3:0] = ALU_code

  // Notes on the sheet:
  //   This circuit is used as a block in the main circuit, and its layout must remain unchanged. The circuit called "main" should be the main circuit of this file.
  //   Do not change the circuit appearance.
  //   DO NOT CHANGE THE INPUTS AND OUTPUTS OF THIS CIRCUIT!
  //   Do not add/remove inputs or outputs. Do not even change their location or orientation.
endmodule

module GEN_0 (
  output [11:0] out_1
);


  assign out_1 = {12{1'b0}};
endmodule

module NOT (
  input  [11:0] in_1,
  output [11:0] out_2
);

  assign out_2 = ~in_1;  // NOT_Gate not_1, 12 bits wide
endmodule

module AND (
  input  [11:0] in_1,
  input  [11:0] in_2,
  output [11:0] out_3
);

  assign out_3 = in_1 & in_2;  // AND_Gate and_1, 12 bits wide
endmodule

module OR (
  input  [11:0] in_1,
  input  [11:0] in_2,
  output [11:0] out_3
);

  assign out_3 = in_1 | in_2;  // OR_Gate or_1, 12 bits wide
endmodule

module ADD (
  input  [11:0] in_1,
  input  [11:0] in_2,
  output [11:0] out_3,
  output OVERFLOW
);

  // OEF_4 oef_4_1: pin names not known; wires that end beside it: in_1, in_2, 1'b0, OVERFLOW, out_3
endmodule

module eq (
  input  [11:0] in_1,
  input  [11:0] in_2,
  output [11:0] out_3
);

  wire and_1_out;
  wire [11:0] xnor_1_out;

  assign xnor_1_out = ~(in_1 ^ in_2);  // XNOR_Gate xnor_1, 12 bits wide
  and and_1 (and_1_out, xnor_1_out[0], xnor_1_out[1], xnor_1_out[2], xnor_1_out[3], xnor_1_out[4], xnor_1_out[5], xnor_1_out[7], xnor_1_out[8], xnor_1_out[9], xnor_1_out[10], xnor_1_out[11], xnor_1_out[6]);
  assign out_3 = {{11{1'b0}}, and_1_out};  // Bit_Extender bit_extender_1
endmodule

module neq (
  input  [11:0] in_1,
  input  [11:0] in_2,
  output [11:0] out_3
);

  wire not_1_out;
  wire [11:0] eq_1_out_3;

  eq eq_1 (.in_1(in_1), .in_2(in_2), .out_3(eq_1_out_3));
  not not_1 (not_1_out, eq_1_out_3[0]);
  assign out_3 = {{11{1'b0}}, not_1_out};  // Bit_Extender bit_extender_1
endmodule

module SUB (
  input  [11:0] in_1,
  input  [11:0] in_2,
  output [11:0] out_3,
  output overflow
);

  wire invert_1_overflow, oef_4_1_p4;
  wire [11:0] invert_1_out_2;

  INVERT invert_1 (.in_1(in_2), .overflow(invert_1_overflow), .out_2(invert_1_out_2));
  xor xor_1 (overflow, invert_1_overflow, oef_4_1_p4);
  // OEF_4 oef_4_1: pin names not known; wires that end beside it: in_1, invert_1_out_2, 1'b0, oef_4_1_p4, out_3
endmodule

module INVERT (
  input  [11:0] in_1,
  output [11:0] out_2,
  output overflow
);

  wire [11:0] not_1_out;

  // Probe on in_1
  assign not_1_out = ~in_1;  // NOT_Gate not_1, 12 bits wide
  // OEF_4 oef_4_1: pin names not known; wires that end beside it: 12'h1, not_1_out, 1'b0, overflow, out_2
  // Probe on out_2
endmodule

module SLL (
  input  [11:0] in_1,
  output [11:0] out_2
);


  assign out_2 = {in_1[10:0], 1'b0};
endmodule

module SRL (
  input  [11:0] in_1,
  output [11:0] out_2
);


  assign out_2 = {1'b0, in_1[11:1]};
endmodule

module NO_OP (
  input  [11:0] in_1,
  output [11:0] out_2
);


  assign out_2 = in_1;
endmodule

module SRA (
  input  [11:0] in_1,
  output [11:0] out_2
);


  assign out_2 = {{2{in_1[11]}}, in_1[10:1]};
endmodule

module SLA (
  input  [11:0] in_1,
  output overflow,
  output [11:0] out_3
);

  xor xor_1 (overflow, in_1[11], in_1[10]);

  assign out_3 = {in_1[10:0], 1'b0};
endmodule

module ABS (
  input  [11:0] in_1,
  output [11:0] out_2
);

  wire [11:0] invert_1_out_2;

  INVERT invert_1 (.in_1(in_1), .out_2(invert_1_out_2));  // open: overflow
  Multiplexer #(.width(12)) multiplexer_1 (.in0(in_1), .in1(invert_1_out_2), .out(out_2), .sel(in_1[11]));  // open: en
endmodule

module GT (
  input  [11:0] in_1,
  input  [11:0] in_2,
  output [11:0] out_3
);

  wire multiplexer_1_out, multiplexer_2_out;
  wire [11:0] abs_1_out_2, abs_2_out_2, eq_1_out_3, sub_1_out_3;

  ABS abs_1 (.in_1(in_1), .out_2(abs_1_out_2));
  eq eq_1 (.in_1(in_2), .in_2(in_1), .out_3(eq_1_out_3));
  ABS abs_2 (.in_1(in_2), .out_2(abs_2_out_2));
  SUB sub_1 (.in_1(abs_1_out_2), .in_2(abs_2_out_2), .out_3(sub_1_out_3));  // open: overflow
  Multiplexer #(.select(3)) multiplexer_1 (
    .in0(1'b1), .in1(1'b0), .in2(1'b1), .in3(1'b1), .in4(1'b0), .in5(1'b0), .in6(1'b0), .in7(1'b1),
    .out(multiplexer_1_out), .sel({in_1[11], in_2[11], sub_1_out_3[11]}));  // open: en
  Multiplexer multiplexer_2 (
    .in0(multiplexer_1_out), .in1(1'b0), .out(multiplexer_2_out), .sel(eq_1_out_3[0]));  // open: en
  assign out_3 = {{11{1'b0}}, multiplexer_2_out};  // Bit_Extender bit_extender_1
endmodule

module LT (
  input  [11:0] in_1,
  input  [11:0] in_2,
  output [11:0] out_3
);

  GT gt_1 (.in_1(in_2), .in_2(in_1), .out_3(out_3));
endmodule
