// Logisim project proj 4.circ as structural Verilog: 4 circuits, main circuit 12-bit register
module _12_bit_register (
  input  clock,
  input  Write,
  input  Reset,
  input  [11:0] Data,
  output [11:0] Register
);

  D_Flip_Flop #(.trigger("falling")) d_ff_1 (
    .clk(clock), .D(Data[3]), .Q(Register[3]), .en(Write), .reset(Reset));  // open: Qn, preset
  D_Flip_Flop #(.trigger("falling")) d_ff_2 (
    .clk(clock), .D(Data[2]), .Q(Register[2]), .en(Write), .reset(Reset));  // open: Qn, preset
  D_Flip_Flop #(.trigger("falling")) d_ff_3 (
    .clk(clock), .D(Data[1]), .Q(Register[1]), .en(Write), .reset(Reset));  // open: Qn, preset
  D_Flip_Flop #(.trigger("falling")) d_ff_4 (
    .clk(clock), .D(Data[0]), .Q(Register[0]), .en(Write), .reset(Reset));  // open: Qn, preset
  D_Flip_Flop #(.trigger("falling")) d_ff_5 (
    .clk(clock), .D(Data[7]), .Q(Register[7]), .en(Write), .reset(Reset));  // open: Qn, preset
  D_Flip_Flop #(.trigger("falling")) d_ff_6 (
    .clk(clock), .D(Data[6]), .Q(Register[6]), .en(Write), .reset(Reset));  // open: Qn, preset
  D_Flip_Flop #(.trigger("falling")) d_ff_7 (
    .clk(clock), .D(Data[5]), .Q(Register[5]), .en(Write), .reset(Reset));  // open: Qn, preset
  D_Flip_Flop #(.trigger("falling")) d_ff_8 (
    .clk(clock), .D(Data[4]), .Q(Register[4]), .en(Write), .reset(Reset));  // open: Qn, preset
  D_Flip_Flop #(.trigger("falling")) d_ff_9 (
    .clk(clock), .D(Data[11]), .Q(Register[11]), .en(Write), .reset(Reset));  // open: Qn, preset
  D_Flip_Flop #(.trigger("falling")) d_ff_10 (
    .clk(clock), .D(Data[10]), .Q(Register[10]), .en(Write), .reset(Reset));  // open: Qn, preset
  D_Flip_Flop #(.trigger("falling")) d_ff_11 (
    .clk(clock), .D(Data[9]), .Q(Register[9]), .en(Write), .reset(Reset));  // open: Qn, preset
  D_Flip_Flop #(.trigger("falling")) d_ff_12 (
    .clk(clock), .D(Data[8]), .Q(Register[8]), .en(Write), .reset(Reset));  // open: Qn, preset
endmodule

module _8_register_file (
  input  [11:0] Data,
  input  Write,
  input  [2:0] rd,
  input  Clock,
  input  Reset,
  input  [2:0] rt,
  input  [2:0] rs,
  output [11:0] T,
  output [11:0] S
);

  wire decoder_1_out1, decoder_1_out2, decoder_1_out3, decoder_1_out4, decoder_1_out5, decoder_1_out6,
       decoder_1_out7;
  wire [11:0] _12_bit_register_2_register, _12_bit_register_3_register, _12_bit_register_4_register,
       _12_bit_register_5_register, _12_bit_register_6_register, _12_bit_register_7_register,
       _12_bit_register_8_register, _12_bit_register_register, undriven;

  Decoder #(.select(3), .disabled(0)) decoder_1 (
    .out1(decoder_1_out1), .out2(decoder_1_out2), .out3(decoder_1_out3), .out4(decoder_1_out4),
    .out5(decoder_1_out5), .out6(decoder_1_out6), .out7(decoder_1_out7), .sel(rd), .en(Write));  // open: out0
  _12_bit_register _12_bit_register (
    .clock(Clock), .Write(1'b0), .Reset(Reset), .Register(_12_bit_register_register), .Data({12{1'b0}}));
  _12_bit_register _12_bit_register_2 (
    .clock(Clock), .Write(decoder_1_out1), .Reset(Reset), .Register(_12_bit_register_2_register), .Data(Data));
  _12_bit_register _12_bit_register_3 (
    .clock(Clock), .Write(decoder_1_out2), .Reset(Reset), .Register(_12_bit_register_3_register),
    .Data(undriven));
  _12_bit_register _12_bit_register_4 (
    .clock(Clock), .Write(decoder_1_out3), .Reset(Reset), .Register(_12_bit_register_4_register), .Data(Data));
  Multiplexer #(.select(3), .width(12)) multiplexer_1 (
    .in0(_12_bit_register_register), .in1(_12_bit_register_2_register), .in2(_12_bit_register_3_register),
    .in3(_12_bit_register_4_register), .in4(_12_bit_register_5_register), .in5(_12_bit_register_6_register),
    .in6(_12_bit_register_7_register), .in7(_12_bit_register_8_register), .out(T), .sel(rt));  // open: en
  Multiplexer #(.select(3), .width(12)) multiplexer_2 (
    .in0(_12_bit_register_register), .in1(_12_bit_register_2_register), .in2(_12_bit_register_3_register),
    .in3(_12_bit_register_4_register), .in4(_12_bit_register_5_register), .in5(_12_bit_register_6_register),
    .in6(_12_bit_register_7_register), .in7(_12_bit_register_8_register), .out(S), .sel(rs));  // open: en
  _12_bit_register _12_bit_register_5 (
    .clock(Clock), .Write(decoder_1_out4), .Reset(Reset), .Register(_12_bit_register_5_register), .Data(Data));
  _12_bit_register _12_bit_register_6 (
    .clock(Clock), .Write(decoder_1_out5), .Reset(Reset), .Register(_12_bit_register_6_register), .Data(Data));
  _12_bit_register _12_bit_register_7 (
    .clock(Clock), .Write(decoder_1_out6), .Reset(Reset), .Register(_12_bit_register_7_register), .Data(Data));
  _12_bit_register _12_bit_register_8 (
    .clock(Clock), .Write(decoder_1_out7), .Reset(Reset), .Register(_12_bit_register_8_register), .Data(Data));
endmodule

module Counter (
  input  CLOCK,
  input  [11:0] DATA,
  output [11:0] out_3
);

  wire comparator_1_lt, not_1_out;
  wire [11:0] oef_3_final_1_sum;

  _12_bit_register u_12_bit_register_1 (
    .clock(CLOCK), .Write(comparator_1_lt), .Reset(not_1_out), .Register(out_3), .Data(oef_3_final_1_sum));
  OEF_3_FINAL oef_3_final_1 (.I(out_3), .I2(12'h1), .in_1(1'b0), .SUM(oef_3_final_1_sum));  // open: overflow
  Comparator #(.width(12)) comparator_1 (.a(out_3), .b(DATA), .lt(comparator_1_lt));  // open: gt, eq
  not not_1 (not_1_out, comparator_1_lt);
endmodule

module Traffic_Light (
);

  wire and_1_out, and_2_out, and_3_out, CLOCK_out, comparator_1_gt, comparator_2_gt, comparator_3_gt,
       comparator_4_gt, comparator_5_gt, not_1_out, or_1_out, or_2_out;
  wire [11:0] COUNTER_out_3;

  Clock CLOCK (.out(CLOCK_out));
  // Probe on COUNTER_out_3
  Counter COUNTER (.CLOCK(CLOCK_out), .DATA(12'h1c), .out_3(COUNTER_out_3));
  Comparator #(.width(12)) comparator_1 (.a(COUNTER_out_3), .b(12'hb), .gt(comparator_1_gt));  // open: eq, lt
  Comparator #(.width(12)) comparator_2 (.a(COUNTER_out_3), .b(12'h7), .gt(comparator_2_gt));  // open: eq, lt
  Comparator #(.width(12)) comparator_3 (.a(COUNTER_out_3), .b(12'hd), .gt(comparator_3_gt));  // open: eq, lt
  Comparator #(.width(12)) comparator_4 (.a(COUNTER_out_3), .b(12'h15), .gt(comparator_4_gt));  // open: eq, lt
  Comparator #(.width(12)) comparator_5 (.a(COUNTER_out_3), .b(12'h19), .gt(comparator_5_gt));  // open: eq, lt
  and and_1 (and_1_out, ~comparator_1_gt, comparator_2_gt);  // AND_Gate
  or or_1 (or_1_out, comparator_1_gt, and_1_out);
  not not_1 (not_1_out, or_1_out);
  and and_2 (and_2_out, comparator_4_gt, ~comparator_5_gt);  // AND_Gate
  LED GROEN (.in(not_1_out));
  LED ORANJE (.in(and_1_out));
  LED ROOD (.in(comparator_1_gt));
  and and_3 (and_3_out, comparator_3_gt, ~comparator_4_gt);  // AND_Gate
  LED GROEN_2 (.in(and_3_out));
  LED ORANJE_2 (.in(and_2_out));
  or or_2 (or_2_out, ~comparator_3_gt, comparator_5_gt);  // OR_Gate
  LED ROOD_2 (.in(or_2_out));
endmodule
