// Logisim project 2FD_Group33.circ as structural Verilog
module main (
  output [11:0] pc,
  output [11:0] r0,
  output [11:0] r1,
  output [11:0] r2,
  output [11:0] r3,
  output [11:0] r4,
  output [11:0] r5,
  output [11:0] r6,
  output [11:0] r7,
  output halt
);

  wire b, blt, branch, branch_pc, clock, clock_1_out, j, jal, jr, jump, memtoreg, memwrite, or_1_out,
       regdest, regwrite, reset, src;
  wire [2:0] multiplexer_1_out, multiplexer_4_out, multiplexer_5_out, multiplexer_6_out, rd, rs, rt;
  wire [3:0] ALU_CODE, decoder_1_function_code, decoder_1_op_code;
  wire [11:0] DATA, imm, multiplexer_2_out, multiplexer_3_out, multiplexer_7_out,
       n8_bit_register_met_outputs_1_s, n8_bit_register_met_outputs_1_t, ram_2_data;
  wire [11:1] jr_pc;
  wire [15:0] ram_1_data;

  Halt halt_1 (.instruction(ram_1_data), .clock(clock_1_out), .reset(reset), .halt(halt));
  Clock clock_1 (.out(clock_1_out));
  Button u_reset (.out(reset));
  _12_bit_program_counter__PC u_12_bit_program_counter_pc_1 (
    .branch_data(pc), .Jump(jump), .imm_value(imm), .reset(reset), .clock(clock), .instruction(pc),
    .jr_pc({jr_pc, b}), .branch(branch_pc), .jr(jr), .j(jal), .j_2(j));
  and and_1 (clock, ~halt, clock_1_out);  // AND_Gate
  and and_2 (branch_pc, branch, b);
  RAM #(.addrWidth(12), .dataWidth(16)) ram_1 (
    .addr(pc), .data(ram_1_data), .clk(clock), .clr(reset));  // open: sel, ld
  // Probe on ram_1_data
  decoder decoder_1 (
    .curr_instr(ram_1_data), .rs(rs), .rd(rd), .op_code(decoder_1_op_code),
    .function_code(decoder_1_function_code), .rt(rt), .immidiate___ta(imm));
  // Probe on imm
  Control_Unit control_unit_1 (
    .OPERATION(decoder_1_op_code), .memToReg(memtoreg), .regDest(regdest), .memWrite(memwrite),
    .ALU_src(src), .FUNCTION(decoder_1_function_code), .ALU_CODE(ALU_CODE), .swicht(branch),
    .regWrite(regwrite), .BLT(blt), .jr(jr), .j(j), .jal(jal), .jump(jump));
  // Probe on imm
  Multiplexer #(.width(3), .enable("false")) multiplexer_1 (
    .in0(rs), .in1(rd), .out(multiplexer_1_out), .sel(or_1_out));
  or or_1 (or_1_out, jr, branch);
  Multiplexer #(.width(12), .enable("false")) multiplexer_2 (
    .in0(n8_bit_register_met_outputs_1_t), .in1(imm), .out(multiplexer_2_out), .sel(src));
  Multiplexer #(.width(12), .enable("false")) multiplexer_3 (
    .in0(multiplexer_2_out), .in1(12'h1), .out(multiplexer_3_out), .sel(jal));
  Multiplexer #(.width(3), .disabled(0), .enable("false")) multiplexer_4 (
    .in0(rt), .in1(rd), .out(multiplexer_4_out), .sel(regdest));
  RAM #(.addrWidth(12), .dataWidth(12), .bus("separate")) ram_2 (
    .addr({jr_pc, b}), .din(n8_bit_register_met_outputs_1_t), .data(ram_2_data), .str(memwrite), .clk(clock),
    .clr(reset));  // open: sel, ld
  Multiplexer #(.width(3), .enable("false")) multiplexer_5 (
    .in0(multiplexer_4_out), .in1(rs), .out(multiplexer_5_out), .sel(branch));
  Multiplexer #(.width(3), .enable("false")) multiplexer_6 (.in0(rd), .in1(3'b111), .out(multiplexer_6_out), .sel(jal));
  Multiplexer #(.width(12), .enable("false")) multiplexer_7 (
    .in0(n8_bit_register_met_outputs_1_s), .in1(pc), .out(multiplexer_7_out), .sel(jal));
  _12_bit_ALU u_12_bit_alu_1 (
    .ALU_code(ALU_CODE), .a(multiplexer_7_out), .b(multiplexer_3_out), .result({jr_pc, b}));  // open: overflow
  Multiplexer #(.width(12), .enable("false")) multiplexer_8 (
    .in0({jr_pc, b}), .in1(ram_2_data), .out(DATA), .sel(memtoreg));
  _8_bit_register_met_outputs u_8_bit_register_met_outputs_1 (
    .Data(DATA), .Write(regwrite), .Clock(clock), .Reset(reset), .rt(multiplexer_5_out),
    .rs(multiplexer_1_out), .r0(r0), .r1(r1), .r2(r2), .r3(r3), .T(n8_bit_register_met_outputs_1_t), .r4(r4),
    .r5(r5), .r6(r6), .r7(r7), .rd(multiplexer_6_out), .S(n8_bit_register_met_outputs_1_s));

  // Other names for the same wires on the sheet: jr_pc[0] = b

  // Notes on the sheet:
  //   current instruction
  //   clock signal
  //   reset button
  //   DO NOT CHANGE THE INPUTS AND OUTPUTS OF THIS CIRCUIT! Do not add/remove inputs or outputs. Do not even change their location or orientation.
endmodule

module Halt (
  input  [15:0] instruction,
  input  clock,
  input  reset,
  output halt
);

  wire and_1_out, comparator_1_eq, comparator_2_gt, counter_1_carry, or_1_out, or_2_out;
  wire [11:0] counter_1_q;

  Comparator #(.width(16), .mode("unsigned")) comparator_1 (
    .a(instruction), .b({16{1'b0}}), .eq(comparator_1_eq));  // open: gt, lt
  Counter #(.width(12), .max('hfff), .trigger("falling")) counter_1 (
    .Q(counter_1_q), .carry(counter_1_carry), .clk(clock), .clr(reset));  // open: load, D, count
  or or_1 (or_1_out, comparator_1_eq, counter_1_carry);
  Comparator #(.width(12), .mode("unsigned")) comparator_2 (
    .a(counter_1_q), .b({12{1'b0}}), .gt(comparator_2_gt));  // open: eq, lt
  or or_2 (or_2_out, halt, and_1_out);
  and and_1 (and_1_out, or_1_out, comparator_2_gt);
  Register #(.width(1)) register_1 (.D(or_2_out), .Q(halt), .clk(clock), .clr(reset));  // open: en

  // Notes on the sheet:
  //   halt becomes and stays asserted if the instruction is 0000 (not in the first clock cycle) or the end of the counter is reached (2^12)
endmodule

module _12_bit_program_counter__PC (
  input  reset,
  input  clock,
  input  [11:0] branch_data,
  input  branch,
  input  Jump,
  input  jr,
  input  [11:0] imm_value,
  input  j,
  input  j_2,
  input  [11:0] jr_pc,
  output [11:0] instruction
);

  wire or_1_out, xor_1_out;
  wire [11:0] add_1_out_3, add_2_out_3, add_3_out_3, add_4_out_3, multiplexer_1_out, multiplexer_2_out,
       multiplexer_3_out, multiplexer_4_out, multiplexer_5_out;

  ADD add_1 (.in_1(instruction), .in_2(branch_data), .out_3(add_1_out_3));  // open: OVERFLOW
  xor xor_1 (xor_1_out, branch, Jump);
  Multiplexer #(.width(12), .enable("false")) multiplexer_1 (
    .in0(add_1_out_3), .in1(branch_data), .out(multiplexer_1_out), .sel(Jump));
  ADD add_2 (.in_1(instruction), .in_2(12'h1), .out_3(add_2_out_3));  // open: OVERFLOW
  ADD add_3 (.in_1(branch_data), .in_2(12'h1), .out_3(add_3_out_3));  // open: OVERFLOW
  Multiplexer #(.width(12), .enable("false")) multiplexer_2 (
    .in0(add_2_out_3), .in1(multiplexer_1_out), .out(multiplexer_2_out), .sel(xor_1_out));
  Multiplexer #(.width(12), .enable("false")) multiplexer_3 (
    .in0(multiplexer_2_out), .in1(add_4_out_3), .out(multiplexer_3_out), .sel(branch));
  ADD add_4 (.in_1(add_3_out_3), .in_2(imm_value), .out_3(add_4_out_3));  // open: OVERFLOW
  Multiplexer #(.width(12), .enable("false")) multiplexer_4 (
    .in0(multiplexer_3_out), .in1(jr_pc), .out(multiplexer_4_out), .sel(jr));
  Multiplexer #(.width(12), .enable("false")) multiplexer_5 (
    .in0(multiplexer_4_out), .in1(imm_value), .out(multiplexer_5_out), .sel(or_1_out));
  or or_1 (or_1_out, j, j_2);
  _12_bit_register u_12_bit_register_1 (
    .clock(clock), .Write(1'b1), .Reset(reset), .Register(instruction), .Data(multiplexer_5_out));
endmodule

module _8_bit_register_met_outputs (
  input  [11:0] Data,
  input  Write,
  input  [2:0] rd,
  input  Clock,
  input  Reset,
  input  [2:0] rt,
  input  [2:0] rs,
  output [11:0] r0,
  output [11:0] r4,
  output [11:0] r5,
  output [11:0] r1,
  output [11:0] r6,
  output [11:0] T,
  output [11:0] r2,
  output [11:0] r7,
  output [11:0] r3,
  output [11:0] S
);

  wire decoder_1_out1, decoder_1_out2, decoder_1_out3, decoder_1_out4, decoder_1_out5, decoder_1_out6,
       decoder_1_out7;

  Decoder #(.select(3), .disabled(0)) decoder_1 (
    .out1(decoder_1_out1), .out2(decoder_1_out2), .out3(decoder_1_out3), .out4(decoder_1_out4),
    .out5(decoder_1_out5), .out6(decoder_1_out6), .out7(decoder_1_out7), .sel(rd), .en(Write));  // open: out0
  _12_bit_register _12_bit_register (.clock(Clock), .Write(1'b0), .Reset(Reset), .Register(r0), .Data({12{1'b0}}));
  _12_bit_register _12_bit_register_2 (
    .clock(Clock), .Write(decoder_1_out1), .Reset(Reset), .Register(r1), .Data(Data));
  _12_bit_register _12_bit_register_3 (
    .clock(Clock), .Write(decoder_1_out2), .Reset(Reset), .Register(r2), .Data(Data));
  _12_bit_register _12_bit_register_4 (
    .clock(Clock), .Write(decoder_1_out3), .Reset(Reset), .Register(r3), .Data(Data));
  Multiplexer #(.select(3), .width(12), .enable("false")) multiplexer_1 (
    .in0(r0), .in1(r1), .in2(r2), .in3(r3), .in4(r4), .in5(r5), .in6(r6), .in7(r7), .out(T), .sel(rt));
  Multiplexer #(.select(3), .width(12), .enable("false")) multiplexer_2 (
    .in0(r0), .in1(r1), .in2(r2), .in3(r3), .in4(r4), .in5(r5), .in6(r6), .in7(r7), .out(S), .sel(rs));
  _12_bit_register _12_bit_register_5 (
    .clock(Clock), .Write(decoder_1_out4), .Reset(Reset), .Register(r4), .Data(Data));
  _12_bit_register _12_bit_register_6 (
    .clock(Clock), .Write(decoder_1_out5), .Reset(Reset), .Register(r5), .Data(Data));
  _12_bit_register _12_bit_register_7 (
    .clock(Clock), .Write(decoder_1_out6), .Reset(Reset), .Register(r6), .Data(Data));
  _12_bit_register _12_bit_register_8 (
    .clock(Clock), .Write(decoder_1_out7), .Reset(Reset), .Register(r7), .Data(Data));
endmodule

module test (
  output [11:0] pc,
  output [11:0] r0,
  output [11:0] r1,
  output [11:0] r2,
  output [11:0] r3,
  output [11:0] r4,
  output [11:0] r5,
  output [11:0] r6,
  output [11:0] r7,
  output halt
);

  wire clock, clock_1_out, comparator_2_eq, IMM, lw, n12_bit_alu_1_p2, not_1_out, reset, select, sw, unary;
  wire [2:0] multiplexer_3_out;
  wire [3:0] CODE, multiplexer_2_out;
  wire [11:0] bit_extender_1_out, data, multiplexer_5_out, n8_bit_register_met_outputs_1_p9,
       n12_bit_alu_1_p3, ram_2_data;
  wire [15:0] ram_1_data;

  Halt halt_1 (.instruction(ram_1_data), .clock(clock_1_out), .reset(reset), .halt(halt));
  Clock clock_1 (.out(clock_1_out));
  Button u_reset (.out(reset));
  // _12_bit_program_counter__PC 12_bit_program_counter_pc_1: pin names not known; wires that end beside it: reset, reset, {12{1'b0}}, 1'b0, 1'b0, reset, clock, pc
  and and_1 (clock, ~halt, clock_1_out);  // AND_Gate
  Comparator #(.width(4)) comparator_1 (.a(ram_1_data[15:12]), .b(4'b1100), .eq(IMM));  // open: gt, lt
  RAM #(.addrWidth(12), .dataWidth(16)) ram_1 (
    .addr(pc), .data(ram_1_data), .clk(clock), .clr(reset));  // open: sel, ld
  Comparator #(.width(4)) comparator_2 (.a(ram_1_data[15:12]), .b(4'b1100), .eq(comparator_2_eq));  // open: gt, lt
  Multiplexer #(.width(4), .enable("false")) multiplexer_1 (
    .in0(multiplexer_2_out), .in1(4'b0100), .out(CODE), .sel(select));
  Comparator #(.width(4)) comparator_3 (.a(ram_1_data[15:12]), .b(4'b0001), .eq(unary));  // open: gt, lt
  Multiplexer #(.width(4), .enable("false")) multiplexer_2 (
    .in0(ram_1_data[15:12]), .in1(ram_1_data[3:0]), .out(multiplexer_2_out), .sel(unary));
  Comparator #(.width(4)) comparator_4 (.a(ram_1_data[15:12]), .b(4'b1010), .eq(lw));  // open: gt, lt
  or or_1 (select, lw, sw);
  Comparator #(.width(4)) comparator_5 (.a(ram_1_data[15:12]), .b(4'b1011), .eq(sw), .lt(sw));  // open: gt
  Multiplexer #(.width(3), .disabled(0), .enable("false")) multiplexer_3 (
    .in0(ram_1_data[2:0]), .in1(ram_1_data[10:8]), .out(multiplexer_3_out), .sel(select));
  assign bit_extender_1_out = {{8{ram_1_data[3]}}, ram_1_data[3:0]};  // Bit_Extender bit_extender_1
  Multiplexer #(.width(12), .enable("false")) multiplexer_4 (
    .in0(n12_bit_alu_1_p3), .in1(ram_2_data), .out(data), .sel(lw));
  Multiplexer #(.width(12), .disabled(0), .enable("false")) multiplexer_5 (
    .in0(n8_bit_register_met_outputs_1_p9), .in1(bit_extender_1_out), .out(multiplexer_5_out), .sel(select));
  // _12_bit_ALU 12_bit_alu_1: pin names not known; wires that end beside it: multiplexer_5_out, n12_bit_alu_1_p2, n12_bit_alu_1_p3, CODE
  not not_1 (not_1_out, sw);
  // _8_bit_register_met_outputs 8_bit_register_met_outputs_1: pin names not known; wires that end beside it: data, not_1_out, clock, reset, multiplexer_3_out, ram_1_data[6:4], n12_bit_alu_1_p2, ram_1_data[10:8], n8_bit_register_met_outputs_1_p9, r0, r1, r2, r3, r4, r5, r6, r4
  RAM #(.addrWidth(12), .dataWidth(12), .bus("separate")) ram_2 (
    .addr(n12_bit_alu_1_p3), .din(n8_bit_register_met_outputs_1_p9), .data(ram_2_data), .str(sw),
    .clk(clock), .ld(lw), .clr(reset));  // open: sel

  // Notes on the sheet:
  //   current instruction
  //   clock signal
  //   reset button
  //   DO NOT CHANGE THE INPUTS AND OUTPUTS OF THIS CIRCUIT! Do not add/remove inputs or outputs. Do not even change their location or orientation.
  //   neit zeker
endmodule

module data_short (
  input  [11:0] alu,
  input  lw,
  input  [11:0] data_in,
  output [11:0] data_out
);

  wire undriven_2;
  wire [11:0] multiplexer_1_out, undriven;

  Multiplexer #(.width(12), .enable("false")) multiplexer_1 (
    .in0(alu), .in1(data_in), .out(multiplexer_1_out), .sel(lw));
  Multiplexer #(.width(12), .enable("false")) multiplexer_2 (
    .in0(multiplexer_1_out), .in1(undriven), .sel(undriven_2));  // open: out
endmodule

module Control_Unit (
  input  [3:0] OPERATION,
  input  [3:0] FUNCTION,
  output memToReg,
  output regDest,
  output [3:0] ALU_CODE,
  output memWrite,
  output ALU_src,
  output swicht,
  output BLT,
  output regWrite,
  output jr,
  output jump,
  output j,
  output jal
);

  wire and_5_out, comparator_3_eq, comparator_4_eq, comparator_5_eq, comparator_6_eq, comparator_8_eq,
       comparator_9_eq, comparator_10_eq, not_1_out, or_3_out;
  wire [3:0] multiplexer_1_out, multiplexer_2_out, multiplexer_3_out;

  Comparator #(.width(4)) comparator_1 (.a(OPERATION), .b(4'b1010), .eq(memToReg));  // open: gt, lt
  Comparator #(.width(4)) comparator_2 (.a(OPERATION), .b(4'b1011), .eq(memWrite));  // open: gt, lt
  Comparator #(.width(4)) comparator_3 (.a(OPERATION), .b(4'b1100), .eq(comparator_3_eq));  // open: gt, lt
  Comparator #(.width(4)) comparator_4 (.a(OPERATION), .b(4'b1101), .eq(comparator_4_eq));  // open: gt, lt
  Comparator #(.width(4)) comparator_5 (.a(OPERATION), .b(4'b0001), .eq(comparator_5_eq));  // open: gt, lt
  Comparator #(.width(4)) comparator_6 (.a(OPERATION), .b(4'b1110), .eq(comparator_6_eq));  // open: gt, lt
  Comparator #(.width(4)) comparator_7 (.a(OPERATION), .b(4'b1111), .eq(BLT));  // open: gt, lt
  Comparator #(.width(4)) comparator_8 (.a(FUNCTION), .b(4'b0010), .eq(comparator_8_eq));  // open: gt, lt
  Comparator #(.width(4)) comparator_9 (.a(FUNCTION), .b(4'b0011), .eq(comparator_9_eq));  // open: gt, lt
  and and_1 (jr, comparator_8_eq, comparator_5_eq);
  and and_2 (j, comparator_9_eq, comparator_5_eq);
  or or_1 (swicht, comparator_6_eq, BLT);
  Comparator #(.width(4)) comparator_10 (.a(FUNCTION), .b(4'b0100), .eq(comparator_10_eq));  // open: gt, lt
  not not_1 (not_1_out, memWrite);
  and and_3 (jal, comparator_10_eq, comparator_5_eq);
  or or_2 (ALU_src, jal, memToReg, memWrite, comparator_3_eq, comparator_4_eq, jr);
  and and_4 (regWrite, ~swicht, ~jr, not_1_out, ~j);  // AND_Gate
  Multiplexer #(.width(4), .enable("false")) multiplexer_1 (
    .in0(FUNCTION), .in1(4'b0100), .out(multiplexer_1_out), .sel(or_3_out));
  or or_3 (or_3_out, memWrite, comparator_3_eq, ALU_src, jal);
  or or_4 (jump, jr, j, jal);
  and and_5 (and_5_out, ~ALU_src, ~comparator_4_eq, ~comparator_5_eq);  // AND_Gate
  Multiplexer #(.width(4), .enable("false")) multiplexer_2 (
    .in0(multiplexer_1_out), .in1(OPERATION), .out(multiplexer_2_out), .sel(and_5_out));
  Multiplexer #(.width(4), .enable("false")) multiplexer_3 (
    .in0(multiplexer_2_out), .in1(4'b1000), .out(multiplexer_3_out), .sel(comparator_6_eq));
  Multiplexer #(.width(4), .enable("false")) multiplexer_4 (
    .in0(multiplexer_3_out), .in1(4'b0110), .out(ALU_CODE), .sel(BLT));

  assign regDest = memWrite;
endmodule

module beq (
  input  [11:0] pc,
  input  [11:0] imm,
  input  [11:0] data,
  output [11:0] new_pc
);

  wire comparator_1_eq;
  wire [11:0] adder_1_out;

  Comparator #(.width(12)) comparator_1 (.a(data), .b(12'h1), .eq(comparator_1_eq));  // open: gt, lt
  Adder #(.width(12)) adder_1 (.a(pc), .b(imm), .out(adder_1_out));  // open: cin, cout
  Adder #(.width(12)) adder_2 (.a(adder_1_out), .b(12'h1));  // open: out, cin, cout
  Multiplexer #(.width(12), .enable("false")) multiplexer_1 (
    .in0(pc), .out(new_pc), .sel(comparator_1_eq));  // open: in1
endmodule

module decoder (
  input  [15:0] curr_instr,
  output [2:0] rs,
  output [2:0] rd,
  output [3:0] op_code,
  output [3:0] function_code,
  output [2:0] rt,
  output [11:0] immidiate___ta
);

  wire and_1_out, and_2_out, and_3_out, comparator_1_eq, comparator_2_eq, comparator_3_eq, comparator_4_eq,
       comparator_5_eq, comparator_6_eq, comparator_7_eq, comparator_8_eq, or_1_out;
  wire [11:0] bit_extender_1_out, bit_extender_2_out, bit_extender_3_out, bit_extender_4_out,
       bit_extender_5_out, multiplexer_1_out, multiplexer_2_out, multiplexer_3_out, multiplexer_6_out,
       multiplexer_7_out;

  Comparator #(.width(4)) comparator_1 (.a(curr_instr[15:12]), .b(4'b0001), .eq(comparator_1_eq));  // open: gt, lt
  Comparator #(.width(4)) comparator_2 (.a(function_code), .b(4'b0011), .eq(comparator_2_eq));  // open: gt, lt
  Comparator #(.width(4)) comparator_3 (.a(function_code), .b(4'b0100), .eq(comparator_3_eq));  // open: gt, lt
  assign bit_extender_1_out = {{8{1'b0}}, curr_instr[3:0]};  // Bit_Extender bit_extender_1
  assign bit_extender_2_out = {{4{curr_instr[7]}}, curr_instr[7:0]};  // Bit_Extender bit_extender_2
  Comparator #(.width(4)) comparator_4 (.a(function_code), .b(4'b0010), .eq(comparator_4_eq));  // open: gt, lt
  Comparator #(.width(4)) comparator_5 (.a(curr_instr[15:12]), .b(4'b1100), .eq(comparator_5_eq));  // open: gt, lt
  Multiplexer #(.width(12), .disabled(0), .enable("false")) multiplexer_1 (
    .in0(bit_extender_1_out), .in1(bit_extender_2_out), .out(multiplexer_1_out), .sel(comparator_5_eq));
  assign bit_extender_3_out = {{8{curr_instr[3]}}, curr_instr[3:0]};  // Bit_Extender bit_extender_3
  and and_1 (and_1_out, comparator_1_eq, comparator_4_eq);
  or or_1 (or_1_out, comparator_2_eq, comparator_3_eq);
  and and_2 (and_2_out, ~curr_instr[13], ~curr_instr[14], ~curr_instr[15]);  // AND_Gate
  Comparator #(.width(4)) comparator_6 (.a(curr_instr[15:12]), .b(4'b1101), .eq(comparator_6_eq));  // open: gt, lt
  Multiplexer #(.width(12), .disabled(0), .enable("false")) multiplexer_2 (
    .in0(multiplexer_1_out), .in1(bit_extender_3_out), .out(multiplexer_2_out), .sel(comparator_6_eq));
  assign bit_extender_4_out = {{8{curr_instr[7]}}, curr_instr[7:4]};  // Bit_Extender bit_extender_4
  and and_3 (and_3_out, comparator_1_eq, or_1_out);
  assign bit_extender_5_out = {{4{1'b0}}, curr_instr[11:4]};  // Bit_Extender bit_extender_5
  Comparator #(.width(4)) comparator_7 (.a(curr_instr[15:12]), .b(4'b1110), .eq(comparator_7_eq));  // open: gt, lt
  Multiplexer #(.width(12), .disabled(0), .enable("false")) multiplexer_3 (
    .in0(multiplexer_2_out), .in1(bit_extender_3_out), .out(multiplexer_3_out), .sel(comparator_7_eq));
  Multiplexer #(.width(4), .disabled(0), .enable("false")) multiplexer_4 (
    .in0(4'b0000), .in1(curr_instr[3:0]), .out(function_code), .sel(and_2_out));
  Multiplexer #(.width(3), .disabled(0), .enable("false")) multiplexer_5 (
    .in0(curr_instr[2:0]), .in1(3'b000), .out(rt), .sel(and_2_out));
  Comparator #(.width(4)) comparator_8 (.a(curr_instr[15:12]), .b(4'b1111), .eq(comparator_8_eq));  // open: gt, lt
  Multiplexer #(.width(12), .disabled(0), .enable("false")) multiplexer_6 (
    .in0(multiplexer_3_out), .in1(bit_extender_3_out), .out(multiplexer_6_out), .sel(comparator_8_eq));
  Multiplexer #(.width(12), .disabled(0), .enable("false")) multiplexer_7 (
    .in0(multiplexer_6_out), .in1(bit_extender_4_out), .out(multiplexer_7_out), .sel(and_1_out));
  Multiplexer #(.width(12), .disabled(0), .enable("false")) multiplexer_8 (
    .in0(multiplexer_7_out), .in1(bit_extender_5_out), .out(immidiate___ta), .sel(and_3_out));

  assign op_code = curr_instr[15:12];
  assign rd = curr_instr[10:8];
  assign rs = curr_instr[6:4];
endmodule
