// Logisim project csa.circ as structural Verilog: 12 circuits, main circuit 4 BIT RCA
module _4_BIT_RCA (
  input  a3,
  input  a2,
  input  a1,
  input  a0,
  input  b3,
  input  b2,
  input  b2_2,
  input  b0,
  input  Carry_In,
  output Carry_Out,
  output s3,
  output s2,
  output s1,
  output s0
);

  wire n1_bit_adder_2_carry_out, n1_bit_adder_3_carry_out, n1_bit_adder_4_carry_out;

  _1_BIT_ADDER u_1_bit_adder_1 (.A(a3), .B(b3), .Carry_In(n1_bit_adder_2_carry_out), .Carry_Out(Carry_Out), .SUM(s3));
  _1_BIT_ADDER u_1_bit_adder_2 (
    .A(a2), .B(b2), .Carry_In(n1_bit_adder_3_carry_out), .Carry_Out(n1_bit_adder_2_carry_out), .SUM(s2));
  _1_BIT_ADDER u_1_bit_adder_3 (
    .A(a1), .B(b2_2), .Carry_In(n1_bit_adder_4_carry_out), .Carry_Out(n1_bit_adder_3_carry_out), .SUM(s1));
  _1_BIT_ADDER u_1_bit_adder_4 (.A(a0), .B(b0), .Carry_In(Carry_In), .Carry_Out(n1_bit_adder_4_carry_out), .SUM(s0));
endmodule

module _1_BIT_ADDER (
  input  Carry_In,
  input  A,
  input  B,
  output SUM,
  output Carry_Out
);

  wire and_1_out, and_2_out, xor_1_out;

  xor xor_1 (xor_1_out, A, B);
  and and_1 (and_1_out, A, B);
  xor xor_2 (SUM, Carry_In, xor_1_out);
  and and_2 (and_2_out, Carry_In, xor_1_out);
  or or_1 (Carry_Out, and_2_out, and_1_out);
endmodule

module _4_bit_adder_FULL (
  input  in_1,
  input  in_2,
  input  in_3,
  input  A0,
  input  in_5,
  input  in_6,
  input  in_7,
  input  B0,
  input  in_9,
  output out_10,
  output s1,
  output s1_2,
  output s1_3,
  output s0,
  output P
);

  wire and_1_out, and_2_out, and_3_out, and_5_out, and_6_out, and_7_out, and_8_out, g0_out, g1_out, g2_out,
       g3_out, or_2_out, or_3_out, or_4_out, or_5_out, p0_out, p1_out, p2_out, p3_out, xor_1_out, xor_4_out,
       xor_5_out, xor_7_out;

  or or_1 (out_10, and_3_out, and_2_out, and_1_out);
  and and_1 (and_1_out, p3_out, g2_out);
  and and_2 (and_2_out, p3_out, p2_out, g1_out);
  and and_3 (and_3_out, p1_out, g0_out, g1_out, p3_out);
  and and_4 (P, g0_out, p3_out, p0_out);
  and g3 (g3_out, in_5, in_1);
  or or_2 (or_2_out, g3_out, and_5_out);
  or p3 (p3_out, in_5, in_1);
  and and_5 (and_5_out, p3_out, or_3_out);
  xor xor_1 (xor_1_out, or_2_out, or_3_out);
  xor xor_2 (s1_2, xor_1_out, p3_out);
  and g2 (g2_out, in_6, in_2);
  or p2 (p2_out, in_6, in_2);
  or or_3 (or_3_out, g2_out, and_6_out);
  xor xor_3 (s1, xor_4_out, p2_out);
  and and_6 (and_6_out, p2_out, or_4_out);
  xor xor_4 (xor_4_out, or_4_out, g2_out);
  and g1 (g1_out, in_7, in_3);
  or or_4 (or_4_out, g1_out, and_7_out);
  or p1 (p1_out, in_7, in_3);
  and and_7 (and_7_out, p1_out, or_5_out);
  xor xor_5 (xor_5_out, g1_out, or_5_out);
  xor xor_6 (s1_3, xor_5_out, p1_out);
  and g0 (g0_out, B0, A0);
  or p0 (p0_out, B0, A0);
  or or_5 (or_5_out, g0_out, and_8_out);
  and and_8 (and_8_out, p0_out, in_9);
  xor xor_7 (xor_7_out, g0_out, in_9);
  xor xor_8 (s0, xor_7_out, p0_out);

  // Notes on the sheet:
  //   (ter illustratie)
endmodule

module _4_bit_adder (
  input  [3:0] A,
  input  CI,
  input  [3:0] B,
  output [3:0] out_4,
  output P0,
  output G0
);

  wire and_1_out, and_2_out, and_3_out, and_4_out, and_5_out, and_6_out, and_7_out, and_8_out, and_9_out,
       g0_out, g1_out, g2_out, g3_out, or_1_out, or_2_out, or_3_out, P0_out, p1_out, p2_out, p3_out;

  and u_g0 (g0_out, A[0], B[0]);
  or u_P0 (P0_out, A[0], B[0]);
  and g1 (g1_out, A[1], B[1]);
  or p1 (p1_out, A[1], B[1]);
  and g2 (g2_out, A[2], B[2]);
  or p2 (p2_out, A[2], B[2]);
  and g3 (g3_out, A[3], B[3]);
  or p3 (p3_out, A[3], B[3]);
  and and_1 (and_1_out, P0_out, CI);
  and and_2 (and_2_out, p1_out, g0_out);
  and and_3 (and_3_out, p1_out, P0_out, CI);
  and and_4 (and_4_out, p2_out, g1_out);
  and and_5 (and_5_out, p2_out, g1_out, g0_out);
  and and_6 (and_6_out, p2_out, p1_out, CI, P0_out);
  and and_7 (and_7_out, g2_out, p3_out);
  and and_8 (and_8_out, g1_out, p3_out, p2_out);
  and and_9 (and_9_out, p3_out, p2_out, p1_out, g0_out);
  or or_1 (or_1_out, g0_out, and_1_out);
  or or_2 (or_2_out, g1_out, and_2_out, and_3_out);
  or or_3 (or_3_out, g2_out, and_4_out, and_5_out, and_6_out);
  and and_10 (P0, P0_out, p2_out, p1_out, p3_out);
  or or_4 (G0, g3_out, and_7_out, and_8_out, and_9_out);
  _1_bit_full_adder_WoCo u_1_bit_full_adder_woco_1 (.C_IN(CI), .A(A[0]), .B(B[0]), .SUM(out_4[0]));
  _1_bit_full_adder_WoCo u_1_bit_full_adder_woco_2 (.C_IN(or_1_out), .A(A[1]), .B(B[1]), .SUM(out_4[1]));
  _1_bit_full_adder_WoCo u_1_bit_full_adder_woco_3 (.C_IN(or_2_out), .A(A[2]), .B(B[2]), .SUM(out_4[2]));
  _1_bit_full_adder_WoCo u_1_bit_full_adder_woco_4 (.C_IN(or_3_out), .A(A[3]), .B(B[3]), .SUM(out_4[3]));
endmodule

module _1_bit_full_adder_WoCo (
  input  C_IN,
  input  A,
  input  B,
  output SUM
);

  wire xor_1_out;

  xor xor_1 (xor_1_out, A, B);
  xor xor_2 (SUM, C_IN, xor_1_out);
endmodule

module CLA (
  input  CI,
  input  g0,
  input  p0,
  input  g1,
  input  p1,
  input  g2,
  input  p2,
  input  g3,
  input  p3,
  output out_10,
  output out_11,
  output out_12,
  output c4,
  output P0_2,
  output G0_2
);

  wire and_1_out, and_2_out, and_3_out, and_4_out, and_5_out, and_6_out, and_7_out, and_8_out, and_9_out,
       and_10_out;

  and and_1 (and_1_out, p0, CI);
  and and_2 (and_2_out, p1, g0);
  and and_3 (and_3_out, p1, p0, CI);
  and and_4 (and_4_out, p2, g1);
  and and_5 (and_5_out, p2, p1, g0);
  and and_6 (and_6_out, p2, p1, CI, p0);
  and and_7 (and_7_out, p3, p1, p0, p2, CI);
  and and_8 (and_8_out, g2, p3);
  and and_9 (and_9_out, g1, p3, p2);
  and and_10 (and_10_out, p3, p2, p1, g0);
  or or_1 (c4, and_8_out, and_9_out, and_10_out, g3, and_7_out);
  or or_2 (out_10, g0, and_1_out);
  or or_3 (out_11, g1, and_2_out, and_3_out);
  or or_4 (out_12, g2, and_4_out, and_5_out, and_6_out);
  and and_11 (P0_2, p0, p2, p1, p3);
  or or_5 (G0_2, g3, and_8_out, and_9_out, and_10_out);
endmodule

module _4_bit_adder__CLA (
  input  [3:0] A,
  input  CI,
  input  [3:0] B,
  output [3:0] SUM,
  output c4,
  output OVERFLOW,
  output G0,
  output P0
);

  wire cla_1_out_10, cla_1_out_11, cla_1_out_12, g0_out, g1_out, g2_out, g3_out, p0_out, p1_out, p2_out,
       p3_out;

  and u_g0 (g0_out, A[0], B[0]);
  or u_p0 (p0_out, A[0], B[0]);
  and g1 (g1_out, A[1], B[1]);
  or p1 (p1_out, A[1], B[1]);
  and g2 (g2_out, A[2], B[2]);
  or p2 (p2_out, A[2], B[2]);
  and g3 (g3_out, A[3], B[3]);
  or p3 (p3_out, A[3], B[3]);
  CLA cla_1 (
    .g0(g0_out), .p0(p0_out), .g1(g1_out), .p1(p1_out), .g2(g2_out), .p2(p2_out), .g3(g3_out), .p3(p3_out),
    .CI(CI), .P0_2(P0), .G0_2(G0), .out_10(cla_1_out_10), .out_11(cla_1_out_11), .out_12(cla_1_out_12),
    .c4(c4));
  xor xor_1 (OVERFLOW, c4, cla_1_out_12);
  _1_bit_full_adder_WoCo u_1_bit_full_adder_woco_1 (.C_IN(CI), .A(A[0]), .B(B[0]), .SUM(SUM[0]));
  _1_bit_full_adder_WoCo u_1_bit_full_adder_woco_2 (.C_IN(cla_1_out_10), .A(A[1]), .B(B[1]), .SUM(SUM[1]));
  _1_bit_full_adder_WoCo u_1_bit_full_adder_woco_3 (.C_IN(cla_1_out_11), .A(A[2]), .B(B[2]), .SUM(SUM[2]));
  _1_bit_full_adder_WoCo u_1_bit_full_adder_woco_4 (.C_IN(cla_1_out_12), .A(A[3]), .B(B[3]), .SUM(SUM[3]));
endmodule

module OEF_3_FINAL (
  input  in_1,
  input  [11:0] I,
  input  [11:0] I2,
  output [11:0] SUM,
  output overflow
);

  wire cla_1_out_10, cla_1_out_11, n4_bit_adder_cla_1_g0, n4_bit_adder_cla_1_p0, n4_bit_adder_cla_2_g0,
       n4_bit_adder_cla_2_p0, n4_bit_adder_cla_3_g0, n4_bit_adder_cla_3_p0;

  // Probe on I
  // Probe on I2
  _4_bit_adder__CLA u_4_bit_adder_cla_1 (
    .A(I[3:0]), .CI(in_1), .B(I2[3:0]), .P0(n4_bit_adder_cla_1_p0), .G0(n4_bit_adder_cla_1_g0), .SUM(SUM[3:0]));  // open: OVERFLOW, c4
  _4_bit_adder__CLA u_4_bit_adder_cla_2 (
    .A(I[7:4]), .CI(cla_1_out_10), .B(I2[7:4]), .P0(n4_bit_adder_cla_2_p0), .G0(n4_bit_adder_cla_2_g0),
    .SUM(SUM[7:4]));  // open: OVERFLOW, c4
  _4_bit_adder__CLA u_4_bit_adder_cla_3 (
    .OVERFLOW(overflow), .A(I[11:8]), .CI(cla_1_out_11), .B(I2[11:8]), .P0(n4_bit_adder_cla_3_p0),
    .G0(n4_bit_adder_cla_3_g0), .SUM(SUM[11:8]));  // open: c4
  // Probe on SUM
  CLA cla_1 (
    .g0(n4_bit_adder_cla_1_g0), .p0(n4_bit_adder_cla_1_p0), .g1(n4_bit_adder_cla_2_g0),
    .p1(n4_bit_adder_cla_2_p0), .g2(n4_bit_adder_cla_3_g0), .p2(n4_bit_adder_cla_3_p0), .CI(in_1),
    .out_10(cla_1_out_10), .out_11(cla_1_out_11));  // open: g3, p3, P0_2, G0_2, out_12, c4
endmodule

module OEF_6 (
  input  [11:0] in_1,
  input  in_2,
  input  [11:0] in_3,
  output [11:0] out_4,
  output out_5,
  output out_6
);

  // Probe on in_1
  // Probe on in_3
  _12_BIT_RCA u_12_bit_rca_1 (
    .in_1(in_1), .in_2(in_3), .carry_in(in_2), .out_6(out_4), .overflow(out_5));  // open: out_4
  OEF_3_FINAL oef_3_final_1 (.I(in_1), .I2(in_3), .in_1(in_2), .overflow(out_6), .SUM(out_4));
  // Probe on out_4
endmodule

module _12_BIT_RCA (
  input  [11:0] in_1,
  input  [11:0] in_2,
  input  carry_in,
  output out_4,
  output overflow,
  output [11:0] out_6
);

  wire n1_bit_adder_lang_1_carry_out, n1_bit_adder_lang_2_carry_out, n1_bit_adder_lang_3_carry_out,
       n1_bit_adder_lang_4_carry_out, n1_bit_adder_lang_5_carry_out, n1_bit_adder_lang_6_carry_out,
       n1_bit_adder_lang_7_carry_out, n1_bit_adder_lang_8_carry_out, n1_bit_adder_lang_9_carry_out,
       n1_bit_adder_lang_10_carry_out, n1_bit_adder_lang_11_carry_out;

  _1_bit_adder_lang u_1_bit_adder_lang_1 (
    .A(in_1[0]), .B(in_2[0]), .Carry_in(carry_in), .SUM(out_6[0]), .Carry_out(n1_bit_adder_lang_1_carry_out));
  _1_bit_adder_lang u_1_bit_adder_lang_2 (
    .A(in_1[1]), .B(in_2[1]), .Carry_in(n1_bit_adder_lang_1_carry_out), .SUM(out_6[1]),
    .Carry_out(n1_bit_adder_lang_2_carry_out));
  _1_bit_adder_lang u_1_bit_adder_lang_3 (
    .A(in_1[2]), .B(in_2[2]), .Carry_in(n1_bit_adder_lang_2_carry_out), .SUM(out_6[2]),
    .Carry_out(n1_bit_adder_lang_3_carry_out));
  _1_bit_adder_lang u_1_bit_adder_lang_4 (
    .A(in_1[3]), .B(in_2[3]), .Carry_in(n1_bit_adder_lang_3_carry_out), .SUM(out_6[3]),
    .Carry_out(n1_bit_adder_lang_4_carry_out));
  _1_bit_adder_lang u_1_bit_adder_lang_5 (
    .A(in_1[4]), .B(in_2[4]), .Carry_in(n1_bit_adder_lang_4_carry_out), .SUM(out_6[4]),
    .Carry_out(n1_bit_adder_lang_5_carry_out));
  _1_bit_adder_lang u_1_bit_adder_lang_6 (
    .A(in_1[5]), .B(in_2[5]), .Carry_in(n1_bit_adder_lang_5_carry_out), .SUM(out_6[5]),
    .Carry_out(n1_bit_adder_lang_6_carry_out));
  _1_bit_adder_lang u_1_bit_adder_lang_7 (
    .A(in_1[6]), .B(in_2[6]), .Carry_in(n1_bit_adder_lang_6_carry_out), .SUM(out_6[6]),
    .Carry_out(n1_bit_adder_lang_7_carry_out));
  _1_bit_adder_lang u_1_bit_adder_lang_8 (
    .A(in_1[7]), .B(in_2[7]), .Carry_in(n1_bit_adder_lang_7_carry_out), .SUM(out_6[7]),
    .Carry_out(n1_bit_adder_lang_8_carry_out));
  _1_bit_adder_lang u_1_bit_adder_lang_9 (
    .A(in_1[8]), .B(in_2[8]), .Carry_in(n1_bit_adder_lang_8_carry_out), .SUM(out_6[8]),
    .Carry_out(n1_bit_adder_lang_9_carry_out));
  _1_bit_adder_lang u_1_bit_adder_lang_10 (
    .A(in_1[9]), .B(in_2[9]), .Carry_in(n1_bit_adder_lang_9_carry_out), .SUM(out_6[9]),
    .Carry_out(n1_bit_adder_lang_10_carry_out));
  _1_bit_adder_lang u_1_bit_adder_lang_11 (
    .A(in_1[10]), .B(in_2[10]), .Carry_in(n1_bit_adder_lang_10_carry_out), .SUM(out_6[10]),
    .Carry_out(n1_bit_adder_lang_11_carry_out));
  _1_bit_adder_lang u_1_bit_adder_lang_12 (
    .A(in_1[11]), .B(in_2[11]), .Carry_in(n1_bit_adder_lang_11_carry_out), .SUM(out_6[11]), .Carry_out(out_4));
  xor xor_1 (overflow, out_4, n1_bit_adder_lang_11_carry_out);

  // Notes on the sheet:
  //   inpyut A
  //   input B
endmodule

module _1_bit_adder_lang (
  input  A,
  input  B,
  input  Carry_in,
  output Carry_out,
  output SUM
);

  wire and_1_out, and_2_out, and_3_out, and_4_out, and_5_out, and_6_out, and_7_out, not_1_out, not_2_out,
       not_3_out;

  not not_1 (not_1_out, A);
  not not_2 (not_2_out, B);
  not not_3 (not_3_out, Carry_in);
  and and_1 (and_1_out, not_1_out, not_2_out, Carry_in);
  and and_2 (and_2_out, not_1_out, B, not_3_out);
  and and_3 (and_3_out, A, not_2_out, not_3_out);
  or or_1 (SUM, and_1_out, and_2_out, and_3_out, and_4_out);
  and and_4 (and_4_out, A, B, Carry_in);
  and and_5 (and_5_out, A, B);
  and and_6 (and_6_out, A, Carry_in);
  and and_7 (and_7_out, B, Carry_in);
  or or_2 (Carry_out, and_5_out, and_6_out, and_7_out);
endmodule

module OEF_4 (
  input  in_1,
  input  [11:0] I,
  input  [11:0] I2,
  output [11:0] SUM,
  output overflow
);

  wire cla_1_out_10, cla_1_out_11, n4_bit_adder_cla_1_g0, n4_bit_adder_cla_1_p0, n4_bit_adder_cla_2_g0,
       n4_bit_adder_cla_2_p0, n4_bit_adder_cla_3_g0, n4_bit_adder_cla_3_p0;

  // Probe on I
  // Probe on I2
  _4_bit_adder__CLA u_4_bit_adder_cla_1 (
    .A(I[3:0]), .CI(in_1), .B(I2[3:0]), .P0(n4_bit_adder_cla_1_p0), .G0(n4_bit_adder_cla_1_g0), .SUM(SUM[3:0]));  // open: OVERFLOW, c4
  _4_bit_adder__CLA u_4_bit_adder_cla_2 (
    .A(I[7:4]), .CI(cla_1_out_10), .B(I2[7:4]), .P0(n4_bit_adder_cla_2_p0), .G0(n4_bit_adder_cla_2_g0),
    .SUM(SUM[7:4]));  // open: OVERFLOW, c4
  _4_bit_adder__CLA u_4_bit_adder_cla_3 (
    .OVERFLOW(overflow), .A(I[11:8]), .CI(cla_1_out_11), .B(I2[11:8]), .P0(n4_bit_adder_cla_3_p0),
    .G0(n4_bit_adder_cla_3_g0), .SUM(SUM[11:8]));  // open: c4
  // Probe on SUM
  CLA cla_1 (
    .g0(n4_bit_adder_cla_1_g0), .p0(n4_bit_adder_cla_1_p0), .g1(n4_bit_adder_cla_2_g0),
    .p1(n4_bit_adder_cla_2_p0), .g2(n4_bit_adder_cla_3_g0), .p2(n4_bit_adder_cla_3_p0), .CI(in_1),
    .out_10(cla_1_out_10), .out_11(cla_1_out_11));  // open: g3, p3, P0_2, G0_2, out_12, c4
endmodule
